# Fritzing sketch schematic (saved by Fritzing 0.9.3b)
breadboards: 2

parts:
  Part1 = Arduino Uno (Rev3) - ICSP
  R1 = Temperature Sensor (Thermistor) [thermistor_type=NTC package=THT]
  R2 = Resistor [tolerance=±5% resistance=10k package="2010 [SMD]"]
  LCD = LCD-16X2 [package=lcd-16x2_noholes]
  LCD_BackLight_resistor = Resistor [tolerance=±5% resistance=2.2k package="2010 [SMD]"]
  LCD_res2 = Resistor [tolerance=±5% resistance=220 package="2010 [SMD]"]
  RGB-LED = RGB LED (com. cathode, rgb) [package="5 mm [THT]"]
  part = Piezo Speaker [part_number=Speaker]
  part_2 = Adafruit ADS1115 16Bit I2C ADC [part_number=AdafruitADS1115]

nets:
  N1: Part1.A0, R1.pin_0, R2.Pin_1, part_2.AIN0
  N2: Part1.A4/SDA, part_2.SDA
  N3: Part1.A5/SCL, part_2.SCL
  VDD: Part1.5V, R1.pin_1, LCD.VDD, LCD_res2.Pin_0, part_2.ADDR, part_2.VDD
  N4: Part1.D8, RGB-LED.red_anode
  N5: Part1.D9_PWM, RGB-LED.green_anode
  N6: Part1.D10_PWM/SS, RGB-LED.blue_anode
  N7: Part1.D11_PWM/MOSI, LCD.E
  N8: Part1.D12/MISO, LCD.RS
  GND: Part1.GND, R2.Pin_0, LCD.VSS, LCD.R_W, LCD.K, LCD_BackLight_resistor.Pin_0, RGB-LED.common_cathode, part.pin2, part_2.GND
  N9: Part1.D2, LCD.DB7
  N10: Part1.D3_PWM, LCD.DB6
  N11: Part1.D4, LCD.DB5
  N12: Part1.D5_PWM, LCD.DB4
  N13: Part1.D7, part.pin1
  N14: LCD.VO, LCD_BackLight_resistor.Pin_1
  N15: LCD.A, LCD_res2.Pin_1

custom parts:
  Adafruit ADS1115 16Bit I2C ADC: For microcontrollers without an analog-to-digital converter or when you want a higher-precision ADC, the ADS1115 provides 16-bit precision at 860 samples/second over I2C. The chip can be configured as 4 single-ended input channels, or two differential channels. As a nice bonus, it even includes a programmable gain amplifier, up to x16, to help boost up smaller single/differential signals to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
